# Fritzing sketch Sketch Two-Sensors-Test (saved by Fritzing 0.9.2b)
breadboards: 2

parts:
  Parte1 = Arduino Uno (Rev3)
  Sensor_1 = SRF05 Ultrasonic Rangefinder
  Sensor_2 = SRF05 Ultrasonic Rangefinder

nets:
  N1: Parte1.D8, Sensor_1.Trig
  N2: Parte1.D10_PWM/SS, Sensor_2.Echo
  N3: Parte1.D11_PWM/MOSI, Sensor_2.Trig
  N4: Parte1.D7, Sensor_1.Echo
  VCC: Parte1.5V, Sensor_1.VCC, Sensor_2.VCC
  GND: Parte1.GND, Sensor_1.GND, Sensor_2.GND
